// Logisim project pong_clock.circ as structural Verilog: 1 circuit, main circuit main
module main (
);

  wire clk, left_edge, nor_1_out, nor_2_out, right_edge;
  wire [3:0] adder_1_out, bit_extender_1_out, register_1_q, xor_1_out;

  Controlled_Buffer controlled_buffer_1 ();  // open: in, out, en
  assign bit_extender_1_out = {{3{nor_1_out}}, nor_1_out};  // Bit_Extender bit_extender_1
  assign xor_1_out = 4'b0001 ^ bit_extender_1_out;  // XOR_Gate xor_1, 4 bits wide
  Adder #(.width(4)) adder_1 (.a(xor_1_out), .b(register_1_q), .out(adder_1_out), .cin(nor_1_out));  // open: cout
  Register #(.width(4)) register_1 (.D(adder_1_out), .en(1'b1), .clk(clk), .Q(register_1_q));  // open: clr
  nor nor_1 (nor_1_out, left_edge, nor_2_out);
  nor nor_2 (nor_2_out, nor_1_out, right_edge);
  Hex_Digit_Display hex_digit_display_1 (.value(register_1_q));  // open: dp
  Comparator #(.width(4)) comparator_1 (.a(register_1_q), .b(4'b0000), .eq(left_edge));  // open: gt, lt
  Comparator #(.width(4)) comparator_2 (.a(register_1_q), .b(4'b0100), .eq(right_edge));  // open: gt, lt
  Clock clock_1 (.out(clk));
endmodule
